# Fritzing sketch wiring-diagram (saved by Fritzing 0.9.3b)
breadboards: 1

parts:
  S1 = Momentary Switch [package=tactile-pth]
  LED1 = smd LED [color="Red (633nm)" package="1206 [SMD]"]
  R1 = Resistor [tolerance=±2% resistance=330 package="0402 [SMD]"]
  Grove1 = Grove OLED 128x96
  Raspberry_Pi1 = Raspberry Pi B+

nets:
  N1: S1.3, R1.Pin_0
  N2: S1.4, Raspberry_Pi1.5V
  GND: LED1.cathode, Grove1.GND, Raspberry_Pi1.GND
  N3: LED1.anode, R1.Pin_1, Raspberry_Pi1.GPIO16
